# Fritzing sketch Umbrella_Dryer_Wiring_Diagram (saved by Fritzing 0.9.3b)
breadboards: 1

parts:
  Part1 = Arduino Uno (Rev3) - ICSP
  RY1 = SSR-40VA
  RY2 = SSR-40VA
  A1 = DHT22 module
  S1 = Momentary Switch [package=ksa_sealed_tac_switch]
  S2 = Momentary Switch [package=ksa_sealed_tac_switch]
  S3 = Momentary Switch [package=ksa_sealed_tac_switch]
  S4 = Momentary Switch [package=ksa_sealed_tac_switch]
  LCD2004-I2C1 = LCD2004-I2C
  F1 = Fan - Ventilador [package=THT]
  R1 = Resistor [tolerance=±5% resistance=220 package="0402 [SMD]"]
  R2 = Resistor [tolerance=±5% resistance=220 package="0402 [SMD]"]
  R3 = Resistor [tolerance=±5% resistance=220 package="0402 [SMD]"]
  R4 = Resistor [tolerance=±5% resistance=220 package="0402 [SMD]"]
  M1 = RioRand LM2596
  HLK-PM1 = HLK-PM12 [part_number=HLK-PM12]
  D1 = Rectifier Diode [part_number=1N4001 package="Melf DO-213 AB [SMD]"]
  C1 = Electrolytic Capacitor [capacitance=100µF package="200 mil [THT, electrolytic]"]
  S5 = D2F-FL Omron Snap Action Limit Switch with Level
  M2 = fc-51 [package=THT]
  A3 = 100w-ptc-air-heater

nets:
  N1: Part1.D8, RY2.Pin_3
  N2: Part1.D9_PWM, RY1.Pin_3
  N3: Part1.D10_PWM/SS, A1.Out
  N4: Part1.D11_PWM/MOSI, M2.pin1
  GND: Part1.GND, RY1.Pin_4, RY2.Pin_4, A1.-, S1.3, S2.3, S3.3, S4.3, LCD2004-I2C1.GND, M1.Pin_4, C1.-, S5.Pin_1, M2.pin2
  N5: Part1.A4/SDA, LCD2004-I2C1.SCL
  N6: Part1.A5/SCL, LCD2004-I2C1.SDA
  N7: Part1.D3_PWM, S5.Pin_2
  N8: Part1.D4, S3.2, R4.Pin_0, R4.Pin_1
  N9: Part1.D5_PWM, S1.2, R3.Pin_0, R3.Pin_1
  N10: Part1.D6_PWM, S2.2, R2.Pin_0, R2.Pin_1
  N11: Part1.D7, S4.2, R1.Pin_0, R1.Pin_1
  5V: Part1.5V, A1.+, LCD2004-I2C1.VCC
  N12: Part1.VIN, D1.cathode, C1.+, M2.pin3
  N13: RY1.Pin_1, F1.5V
  N14: RY1.Pin_2, RY2.Pin_2, HLK-PM1.AC_2
  N15: RY2.Pin_1, A3.Pin_1
  N16: F1.GND, HLK-PM1.AC_1, A3.Pin_2
  N17: M1.Pin_1, HLK-PM1.+Vo
  N18: M1.Pin_2, HLK-PM1.-Vo
  N19: M1.Pin_3, D1.anode

custom parts:
  SSR-40VA: SSR-40VA solid state relay.
  DHT22 module: DHT22 module. Pins VCC Data GND.
  LCD2004-I2C: A standard character display with 4x20 characters. Comes in many colors with LCM2004 IIC attached.
  Fan - Ventilador: Ventilador de 2 pines, se encuentra comunmente en computadoras de escritorio
  D2F-FL Omron Snap Action Limit Switch with Level: Snap action switch with stainless steel lever.
  100w-ptc-air-heater: 110V 100W Surface Insulated PTC Air Heater PTC Heating Element Incubator Controller Incubation Heater.
